# Fritzing sketch scheme (saved by Fritzing 0.9.10b)

parts:
  Компонент1 = Arduino Nano (Rev3.0)
  Компонент2 = LCD1602-I2C
  R1 = Resistor [tolerance=±5% resistance=100 power=0.25 package=THT]
  R3 = Resistor [tolerance=±5% resistance=10k package="0805 [SMD]"]
  M1 = DC Motor [voltage_(max)=6V voltage_(min)=3V]
  M2 = DC Motor [voltage_(max)=6V voltage_(min)=3V]
  Power_plug1 = Power plug
  R5 = Resistor [tolerance=±5% resistance=10k power=0.5W package="0603 [SMD]"]
  S1 = Pushbutton [package="[THT]"]
  S2 = Pushbutton [package="[THT]"]
  R4 = Resistor [tolerance=±5% power=0.25 resistance=100 package=THT]
  Q3 = Basic FET N-Channel [package="DPak [SMD]"]
  Q4 = Basic FET N-Channel [package="DPak [SMD]"]

nets:
  GND: Компонент1.GND, Power_plug1.GND
  N1: Компонент1.D7, R4.Pin_1
  N2: Компонент1.D8, R1.Pin_1
  N3: Компонент1.D11/MOSI, S1.Pin_3
  N4: Компонент1.D12/MISO, S2.Pin_3
  N5: Компонент1.A5, Компонент2.SCL
  N6: Компонент1.A4, Компонент2.SDA
  N7: R1.Pin_0, R3.Pin_1
  N8: R3.Pin_0, Q4.Gate
  N9: M1.pin_2, Q3.drain
  N10: M2.pin_2, Q4.drain
  N11: R5.Pin_0, Q3.Gate
  N12: R5.Pin_1, R4.Pin_0

notes:
  Помпы 5В
  Источник питания 5В
  Кнопки для управления дисплеем
  100Ω
  10kΩ

custom parts:
  LCD1602-I2C: A standard character display, usually with 2x16 characters. Comes in many colors with LCM1602 IIC attached.
